# Fritzing sketch sketch_gtab (saved by Fritzing 0.9.3b)
breadboards: 1

parts:
  MH-ET_LIVE_ESP32_DEVKIT1 = MH-ET LIVE ESP32 DEVKIT 38 pins
  Componente1 = 3.5in TFT 480x320 Touch + MicroSD
  Componente2 = Thumb Joystick
  S1 = Momentary Switch [package=ksa_sealed_tac_switch]
  R1 = Resistor [tolerance=±5% resistance=220 package="0402 [SMD]"]
  Componente3 = LCD1602-I2C

nets:
  3V3: MH-ET_LIVE_ESP32_DEVKIT1.3V3, Componente1.3-5V, Componente1.+5V, Componente2.VCC, S1.1
  N1: MH-ET_LIVE_ESP32_DEVKIT1.IO34, Componente2.VERT
  N2: MH-ET_LIVE_ESP32_DEVKIT1.IO35, Componente2.HORZ
  N3: MH-ET_LIVE_ESP32_DEVKIT1.IO25, Componente2.SEL
  N4: MH-ET_LIVE_ESP32_DEVKIT1.IO27, Componente1.LCD_RS_5V
  N5: MH-ET_LIVE_ESP32_DEVKIT1.IO14, Componente1.LCD_CS_5V
  5V: MH-ET_LIVE_ESP32_DEVKIT1.5V, Componente3.VCC
  GND: MH-ET_LIVE_ESP32_DEVKIT1.GND, Componente1.GND, R1.Pin_0
  N6: MH-ET_LIVE_ESP32_DEVKIT1.IO23, Componente1.MOSI
  N7: MH-ET_LIVE_ESP32_DEVKIT1.IO22, Componente3.SCL
  N8: MH-ET_LIVE_ESP32_DEVKIT1.IO21, Componente3.SDA
  N9: MH-ET_LIVE_ESP32_DEVKIT1.IO19, Componente1.MISO
  N10: MH-ET_LIVE_ESP32_DEVKIT1.IO18, Componente1.LCD_WR_5V
  N11: MH-ET_LIVE_ESP32_DEVKIT1.IO2, S1.4
  N12: MH-ET_LIVE_ESP32_DEVKIT1.IO15, Componente1.LCD_RST_5V
  GND_2: Componente2.GND, Componente3.GND
  N13: S1.3, R1.Pin_1

custom parts:
  MH-ET LIVE ESP32 DEVKIT 38 pins: http://mh.nodebb.com/topic/2/mh-et-live-esp32-devkit
  3.5in TFT 480x320 Touch + MicroSD: This TFT display is big (3.5" diagonal), bright (6 white-LED backlight) and colorful! 480x320 pixels with individual RGB pixel control. This display also has a resistive touchscreen attached to it already, so you can detect finger presses anywhere on the screen. There is a controller built into the display with RAM buffering, so that almost no work is done by the microcontroller. The display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
  LCD1602-I2C: A standard character display, usually with 2x16 characters. Comes in many colors with LCM1602 IIC attached.
